// Logisim project 1bit_CPU.circ as structural Verilog: 2 circuits, main circuit One_Bit_CPU
module One_Bit_CPU (
  input  Reset,
  input  Clock,
  input  DataIn,
  input  [7:0] InstructionIn,
  output DataOut,
  output Write,
  output [10:0] DataAddress,
  output [11:0] InstructionAddress
);

  wire Accumulator_q, bitselector_1_out, Clk2, FetchNext_qn, not_3_out, xor_1_out;
  wire [2:0] StackPointer_q;
  wire [3:0] and_1_out;
  wire [6:0] FetchNext_q;
  wire [11:0] InstructionRegister_q, multiplexer_1_out, ProgramStack_dout;
  wire [17:0] Microcode_data;

  not not_1 (Clk2, Clock);
  ROM #(.addrWidth(7), .dataWidth(18)) Microcode (
    .addr({FetchNext_q[6:3], InstructionRegister_q[11:10], FetchNext_q[0]}), .data(Microcode_data));
  Counter #(.max('h7), .width(3)) StackPointer (
    .clr(Reset), .load(Microcode_data[16]), .up(Microcode_data[17]), .count(1'b1), .clk(Clock),
    .Q(StackPointer_q));  // open: D, carry
  // Probe on Microcode_data
  and and_1 (and_1_out[0], and_1_out[3], Accumulator_q);
  or or_1 (and_1_out[1], and_1_out[3], Accumulator_q);
  not not_2 (and_1_out[2], Accumulator_q);
  RAM #(.addrWidth(3), .dataWidth(12)) ProgramStack (
    .addr(StackPointer_q), .we(Microcode_data[14]), .oe(Microcode_data[15]), .din(InstructionAddress),
    .dout(ProgramStack_dout));  // open: clk
  T_Flip_Flop FetchNext (
    .T(Microcode_data[13]), .clk(Clock), .Q(FetchNext_q[0]), .Qn(FetchNext_qn), .reset(Reset));  // open: preset
  // Probe on Microcode_data[4]
  // Probe on Microcode_data[5]
  // Probe on xor_1_out
  Register #(.width(1)) Accumulator (
    .D(bitselector_1_out), .en(Microcode_data[3]), .clk(Clk2), .Q(Accumulator_q), .clr(Reset));
  BitSelector #(.width(7)) bitselector_1 (
    .in({2'b01, DataIn, and_1_out}), .out(bitselector_1_out), .sel(Microcode_data[2:0]));
  Register ExtraByte (.D(InstructionIn), .en(FetchNext_q[0]), .clk(Clock), .Q(InstructionRegister_q[7:0]), .clr(Reset));
  Register InstructionRegister (
    .D(InstructionIn), .en(FetchNext_qn), .clk(Clock), .Q({FetchNext_q[6:3], InstructionRegister_q[11:8]}),
    .clr(Reset));
  xor xor_1 (xor_1_out, Microcode_data[5], Clk2);
  Multiplexer #(.width(12)) multiplexer_1 (
    .in0(InstructionRegister_q), .in1(ProgramStack_dout), .out(multiplexer_1_out), .sel(Microcode_data[12]));
  // Probe on {FetchNext_q[3], InstructionRegister_q[11:8]}
  RAM #(.addrWidth(5), .dataWidth(1)) Registers (
    .addr({FetchNext_q[3], InstructionRegister_q[11:8]}), .we(Microcode_data[4]), .oe(Microcode_data[5]),
    .clk(xor_1_out), .din(Accumulator_q), .dout(and_1_out[3]));
  Counter #(.max('hfff), .width(12)) ProgramCounter (
    .clr(Reset), .load(Microcode_data[10]), .up(not_3_out), .count(1'b1), .clk(Clk2), .D(multiplexer_1_out),
    .Q(InstructionAddress));  // open: carry
  not not_3 (not_3_out, Microcode_data[11]);
  Counter #(.max('h7ff), .width(11)) AddressLatch_IncDec (
    .clr(Reset), .load(Microcode_data[8]), .up(Microcode_data[9]), .count(1'b1), .clk(Clk2),
    .D(InstructionRegister_q[10:0]), .Q(DataAddress));  // open: carry
  // Probe on and_1_out[3]
  Register #(.width(1)) DataOutLatch (.D(Accumulator_q), .en(Microcode_data[6]), .clk(Clk2), .Q(DataOut), .clr(Reset));
  Register #(.width(1)) WriteLatch (
    .D(InstructionRegister_q[11]), .en(Microcode_data[7]), .clk(Clk2), .Q(Write), .clr(Reset));

  // Other names for the same wires on the sheet: Clk1 = Clock; Rst = Reset

  // Notes on the sheet:
  //   contents of Microcode (hex, n*v repeats v):
  //   8 0 8 0 8 0 8 0 8 0 8 0 8 0 8 0 9 0 9 0 9 0 9 0 9 0 9 0 9 0 9 0 2b 0 2b 0 2b 0 2b 0 2b 0 2b 0 2b 0
  //   2b 0 10 0 10 0 10 0 10 0 10 0 10 0 10 0 10 0 a 0 0 0 e 0 d
endmodule

module CPU_and_ProgramRom (
);

  wire MasterClock_out, por_1_out;
  wire [7:0] ProgramROM_data;
  wire [11:0] one_bit_cpu_1_instructionaddress;

  Clock #(.highDuration(2), .lowDuration(2)) MasterClock (.out(MasterClock_out));
  POR por_1 (.out(por_1_out));
  ROM #(.addrWidth(12)) ProgramROM (.addr(one_bit_cpu_1_instructionaddress), .data(ProgramROM_data));
  One_Bit_CPU one_bit_cpu_1 (
    .Reset(por_1_out), .Clock(MasterClock_out), .InstructionIn(ProgramROM_data),
    .InstructionAddress(one_bit_cpu_1_instructionaddress));  // open: DataIn, DataOut, Write, DataAddress

  // Notes on the sheet:
  //   contents of ProgramROM (hex, n*v repeats v):
  //   8c 60 41 40 41 40
endmodule
